// Logisim project traffic_light_simulator.circ as structural Verilog: 1 circuit, main circuit main
module main (
);

  wire clock_1_out;
  wire [9:0] counter_1_q;
  wire [18:0] rom_1_data;

  Counter #(.width(10), .max('h3ff)) counter_1 (
    .Q(counter_1_q), .clk(clock_1_out));  // open: load, D, count, carry, clr
  Clock clock_1 (.out(clock_1_out));
  ROM #(.addrWidth(10), .dataWidth(19)) rom_1 (.addr(counter_1_q), .data(rom_1_data), .sel(1'b1));
  _7_Segment_Display u_7_segment_display_1 (
    .g(rom_1_data[18]), .f(rom_1_data[17]), .a(rom_1_data[12]), .b(rom_1_data[13]), .e(rom_1_data[16]),
    .d(rom_1_data[15]), .c(rom_1_data[14]));  // open: dp
  LED led_1 (.in(rom_1_data[2]));
  LED led_2 (.in(rom_1_data[3]));
  LED led_3 (.in(rom_1_data[4]));
  _7_Segment_Display u_7_segment_display_2 (
    .g(rom_1_data[11]), .f(rom_1_data[10]), .a(rom_1_data[5]), .b(rom_1_data[6]), .e(rom_1_data[9]),
    .d(rom_1_data[8]), .c(rom_1_data[7]));  // open: dp
  LED led_4 (.in(rom_1_data[0]));
  LED led_5 (.in(rom_1_data[1]));

  // Notes on the sheet:
  //   contents of rom_1 (hex, n*v repeats v):
  //   00005 00005 00005 00005 00005 00005 00005 00005  00005 00005 00005 00005 00006 00006 00006 00006
  //   00006 00006 00006 00006 00006 00006 00006 00006  00006 00006 00006 00006 00006 00006 00006 00006
  //   00006 00006 00006 00006 00006 00006 00006 00006  00006 00006 00006 00006 00006 00006 00006 00006
  //   00006 00006 00006 00006 00006 00006 00006 00006  00006 00006 00006 00006 00006 00006 00006 00006
  //   00006 00006 00006 00006 00006 00006 00006 00006  00006 00006 00006 00006 00006 00006 00006 00006
  //   00006 00006 00006 00006 00005 00005 00005 00005  00005 00005 00005 00005 00005 00005 00005 00005
  //   00005 00005 00005 00005 0000D 0000D 0000D 0000D  0000D 0000D 0000D 0000D 5B0D1 5B0D1 5B0D1 5B0D1
  //   5B0D1 5B0D1 5B0D1 5B0D1 5B7F1 5B7F1 5B7F1 5B7F1  5B7F1 5B7F1 5B7F1 5B7F1 06DF1 06DF1 06DF1 06DF1
  //   06DF1 06DF1 06DF1 06DF1 06FF1 06FF1 06FF1 06FF1  06FF1 06FF1 06FF1 06FF1 060F1 060F1 060F1 060F1
  //   060F1 060F1 060F1 060F1 06FB1 06FB1 06FB1 06FB1  06FB1 06FB1 06FB1 06FB1 06DB1 06DB1 06DB1 06DB1
  //   06DB1 06DB1 06DB1 06DB1 06CD1 06CD1 06CD1 06CD1  06CD1 06CD1 06CD1 06CD1 069F1 069F1 069F1 069F1
  //   069F1 069F1 069F1 069F1 06B71 06B71 06B71 06B71  06B71 06B71 06B71 06B71 060D1 060D1 060D1 060D1
  //   060D1 060D1 060D1 060D1 067F1 067F1 067F1 067F1  067F1 067F1 067F1 067F1 00DF1 00DF1 00DF1 00DF1
  //   00DF1 00DF1 00DF1 00DF1 00FF1 00FF1 00FF1 00FF1  00FF1 00FF1 00FF1 00FF1 000F1 000F1 000F1 000F1
  //   000F1 000F1 000F1 000F1 00FB1 00FB1 00FB1 00FB1  00FB1 00FB1 00FB1 00FB1 00DB1 00DB1 00DB1 00DB1
  //   00DB1 00DB1 00DB1 00DB1 00CD1 00CD1 00CD1 00CD1  00CD1 00CD1 00CD1 00CD1 009F1 009F1 009F1 009F1
  //   009F1 009F1 009F1 009F1 00B71 00B71 00B71 00B71  00B71 00B71 00B71 00B71 000D1 000D1 000D1 000D1
  //   000D1 000D1 000D1 000D1 007F1 007F1 007F1 007F1  007F1 007F1 007F1 007F1 00009 00009 00009 00009
  //   00009 00009 00009 00009 00005 00005 00005 00005  00005 00005 00005 00005 00005 00005 00005 00005
  //   00005 00005 00005 00005 00006 00006 00006 00006  00006 00006 00006 00006 00006 00006 00006 00006
  //   00006 00006 00006 00006 00006 00006 00006 00006  00006 00006 00006 00006 00006 00006 00006 00006
  //   00006 00006 00006 00006 00006 00006 00006 00006  00006 00006 00006 00006 00006 00006 00006 00006
  //   00006 00006 00006 00006 00006 00006 00006 00006  00006 00006 00006 00006 00006 00006 00006 00006
  //   00006 00006 00006 00006 00006 00006 00006 00006  00006 00006 00006 00006 00005 00005 00005 00005
  //   00005 00005 00005 00005 00005 00005 00005 00005  00005 00005 00005 00005 0000D 0000D 0000D 0000D
  //   0000D 0000D 0000D 0000D 5B0D1 5B0D1 5B0D1 5B0D1  5B0D1 5B0D1 5B0D1 5B0D1 5B7F1 5B7F1 5B7F1 5B7F1
  //   5B7F1 5B7F1 5B7F1 5B7F1 06DF1 06DF1 06DF1 06DF1  06DF1 06DF1 06DF1 06DF1 06FF1 06FF1 06FF1 06FF1
  //   06FF1 06FF1 06FF1 06FF1 060F1 060F1 060F1 060F1  060F1 060F1 060F1 060F1 06FB1 06FB1 06FB1 06FB1
  //   06FB1 06FB1 06FB1 06FB1 06DB1 06DB1 06DB1 06DB1  06DB1 06DB1 06DB1 06DB1 06CD1 06CD1 06CD1 06CD1
  //   06CD1 06CD1 06CD1 06CD1 069F1 069F1 069F1 069F1  069F1 069F1 069F1 069F1 06B71 06B71 06B71 06B71
  //   06B71 06B71 06B71 06B71 060D1 060D1 060D1 060D1  060D1 060D1 060D1 060D1 067F1 067F1 067F1 067F1
  //   067F1 067F1 067F1 067F1 00DF1 00DF1 00DF1 00DF1  00DF1 00DF1 00DF1 00DF1 00FF1 00FF1 00FF1 00FF1
  //   00FF1 00FF1 00FF1 00FF1 000F1 000F1 000F1 000F1  000F1 000F1 000F1 000F1 00FB1 00FB1 00FB1 00FB1
  //   00FB1 00FB1 00FB1 00FB1 00DB1 00DB1 00DB1 00DB1  00DB1 00DB1 00DB1 00DB1 00CD1 00CD1 00CD1 00CD1
  //   00CD1 00CD1 00CD1 00CD1 009F1 009F1 009F1 009F1  009F1 009F1 009F1 009F1 00B71 00B71 00B71 00B71
  //   00B71 00B71 00B71 00B71 000D1 000D1 000D1 000D1  000D1 000D1 000D1 000D1 007F1 007F1 007F1 007F1
  //   007F1 007F1 007F1 007F1 00009 00009 00009 00009  00009 00009 00009 00009 00005 00005 00005 00005
  //   00005 00005 00005 00005 00005 00005 00005 00005  00005 00005 00005 00005 00006 00006 00006 00006
  //   00006 00006 00006 00006 00006 00006 00006 00006  00006 00006 00006 00006 00006 00006 00006 00006
  //   00006 00006 00006 00006 00006 00006 00006 00006  00006 00006 00006 00006 00006 00006 00006 00006
  //   00006 00006 00006 00006 00006 00006 00006 00006  00006 00006 00006 00006 00006 0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
endmodule
